# Fritzing sketch bubble (saved by Fritzing 0.9.3b)
circuit board: 3.72944cm x 1.99843cm
breadboards: 1

parts:
  SEG1 = 7-Segment Bubble Display [part_number=COM-12710 package="DIP (Dual Inline) [THT]"]
  U1 = MAX7219 [package=dil24]

nets:
  N1: SEG1.C1, U1.DIG0
  N2: SEG1.Ae, U1.SEGE
  N3: SEG1.Ac, U1.SEGC
  N4: SEG1.C3, U1.DIG2
  N5: SEG1.Adp, U1.SEGDP
  N6: SEG1.C4, U1.DIG3
  N7: SEG1.Ag, U1.SEGG
  N8: SEG1.Ad, U1.SEGD
  N9: SEG1.Af, U1.SEGF
  N10: SEG1.C2, U1.DIG1
  N11: SEG1.Ab, U1.SEGB
  N12: SEG1.Aa, U1.SEGA

custom parts:
  7-Segment Bubble Display: This is the HP QDSP-6064 bubble display, a tiny, 4-digit, 7-segment numerical indicator. THis little guy is perfect if you need some user feedback from your system, but don’t want to fiddle with LCDs or other display options. The Bubble Display comes in an easy-to-use 12-pin DIP package and can be used in breadboards, protoboards, or PCBs.
